// Logisim project CSE-231-Lab-5-Logisim.circ as structural Verilog
module Lab_5 (
  input  m,
  input  [3:0] A,
  input  [3:0] in_3,
  output [3:0] out_4
);

  wire [3:0] xor_1_out;

  xor xor_1 (xor_1_out[0], in_3[0], m);
  xor xor_2 (xor_1_out[1], m, in_3[1]);
  xor xor_3 (xor_1_out[2], in_3[2], m);
  xor xor_4 (xor_1_out[3], in_3[3], m);
  Adder #(.width(4)) adder_1 (.a(A), .b(xor_1_out), .out(out_4), .cin(m));  // open: cout
endmodule

module Cir_2 (
  input  [3:0] in_1,
  input  [3:0] in_2,
  input  in_3,
  output out_4,
  output [3:0] out_5
);

  wire adder_1_cout, and_1_out, and_2_out, or_2_out;
  wire [3:0] adder_1_out;

  or or_1 (out_4, adder_1_cout, or_2_out);
  or or_2 (or_2_out, and_1_out, and_2_out);
  Adder #(.width(4)) adder_1 (.a(in_1), .b(in_2), .out(adder_1_out), .cin(in_3), .cout(adder_1_cout));
  and and_1 (and_1_out, adder_1_out[3], adder_1_out[2]);
  and and_2 (and_2_out, adder_1_out[3], adder_1_out[1]);
  Adder #(.width(4)) adder_2 (.a({in_3, {2{out_4}}, in_3}), .b(adder_1_out), .out(out_5), .cin(in_3));  // open: cout
endmodule
