// Logisim project D- Flip-Flop.circ as structural Verilog: 1 circuit, main circuit D - Flip-Flop
module D___Flip_Flop (
  input  in_1,
  output out_2,
  output out_3,
  output Y
);

  wire and_1_out, and_2_out, and_3_out, clock_1_out, d_ff_1_qn, d_ff_2_qn, not_1_out, or_1_out;

  not not_1 (not_1_out, in_1);
  and and_1 (and_1_out, out_2, not_1_out);
  and and_2 (and_2_out, in_1, d_ff_1_qn);
  or or_1 (or_1_out, and_1_out, and_2_out);
  Clock clock_1 (.out(clock_1_out));
  D_Flip_Flop d_ff_1 (.clk(clock_1_out), .D(or_1_out), .Q(out_2), .Qn(d_ff_1_qn));  // open: preset, en, reset
  and and_3 (and_3_out, not_1_out, d_ff_1_qn);
  D_Flip_Flop d_ff_2 (.clk(clock_1_out), .D(and_3_out), .Q(out_3), .Qn(d_ff_2_qn));  // open: preset, en, reset
  and and_4 (Y, in_1, d_ff_1_qn);
endmodule
