// Logisim project J-K - Flip-Flop.circ as structural Verilog: 1 circuit, main circuit J-K-Flip-Flop
module J_K_Flip_Flop (
  input  X,
  output out_2,
  output out_3,
  output Y
);

  wire and_1_out, clock_1_out, j_k_ff_1_qn, j_k_ff_2_qn, not_1_out;

  not not_1 (not_1_out, X);
  Clock clock_1 (.out(clock_1_out));
  J_K_Flip_Flop_part j_k_ff_1 (
    .J(X), .clk(clock_1_out), .K(X), .Q(out_2), .Qn(j_k_ff_1_qn));  // open: preset, en, reset
  and and_1 (and_1_out, not_1_out, j_k_ff_1_qn);
  J_K_Flip_Flop_part j_k_ff_2 (
    .J(and_1_out), .clk(clock_1_out), .K(X), .Q(out_3), .Qn(j_k_ff_2_qn));  // open: preset, en, reset
  and and_2 (Y, X, j_k_ff_1_qn);
endmodule
