// Logisim project T -Flip-Flop.circ as structural Verilog: 1 circuit, main circuit T -Flip-Flop
module T__Flip_Flop (
  input  X,
  output out_2,
  output out_3,
  output Y
);

  wire and_1_out, and_2_out, clock_1_out, not_1_out, or_1_out, t_ff_1_qn, t_ff_2_qn;

  not not_1 (not_1_out, X);
  Clock clock_1 (.out(clock_1_out));
  T_Flip_Flop t_ff_1 (.clk(clock_1_out), .T(X), .Q(out_2), .Qn(t_ff_1_qn));  // open: preset, reset, en
  and and_1 (and_1_out, out_3, X);
  or or_1 (or_1_out, and_1_out, and_2_out);
  and and_2 (and_2_out, t_ff_1_qn, t_ff_2_qn, not_1_out);
  T_Flip_Flop t_ff_2 (.clk(clock_1_out), .T(or_1_out), .Q(out_3), .Qn(t_ff_2_qn));  // open: preset, reset, en
  and and_3 (Y, X, t_ff_1_qn);

  // Notes on the sheet:
  //      CLK
endmodule
